// Logisim project hw4.circ as structural Verilog: 3 circuits, main circuit main
module main (
);

  D_Flip_Flop d_ff_1 ();  // open: clk, D, Q, Qn, preset, reset
  ROM Instruction_Memory_b2d019ad ();  // open: addr, data
  RAM Data_Memory_704a74f6 ();  // open: addr, data, sel, clk, ld, clr
endmodule

module RegisterFile (
);

  CreateRegister createregister_1 ();  // open: Data, out_2
  CreateRegister createregister_2 ();  // open: Data, out_2
  CreateRegister createregister_3 ();  // open: Data, out_2
  CreateRegister createregister_4 ();  // open: Data, out_2
  CreateRegister createregister_5 ();  // open: Data, out_2
  CreateRegister createregister_6 ();  // open: Data, out_2
  CreateRegister createregister_7 ();  // open: Data, out_2
  CreateRegister createregister_8 ();  // open: Data, out_2
endmodule

module CreateRegister (
  input  [2:0] Data,
  output [2:0] out_2
);

  wire clock_1_out;

  Clock clock_1 (.out(clock_1_out));
  D_Flip_Flop d_ff_1 (.D(Data[0]), .clk(clock_1_out), .Q(out_2[0]));  // open: Qn, preset, reset
  D_Flip_Flop d_ff_2 (.D(Data[1]), .clk(clock_1_out), .Q(out_2[1]));  // open: Qn, preset, reset
  D_Flip_Flop d_ff_3 (.D(Data[2]), .clk(clock_1_out), .Q(out_2[2]));  // open: Qn, preset, reset
endmodule
